# Fritzing sketch skv_v12-arduino-pro-mini-1 (saved by Fritzing 0.8.7b)
circuit board: 4.83449cm x 4.23615cm

parts:
  LCD = LCD screen
  DS2 = DS18B20 1-Wire Temperature Sensor [part_number=DS18B20]
  Rele = Relay [part_number=FRS1B-S package=THT]
  DS1 = DS18B20 1-Wire Temperature Sensor [part_number=DS18B20]
  Rele1 = Relay [part_number=FRS1B-S package=THT]
  4k7 = 4k7 Ω Resistor [package=THT]
  DS3 = DS18B20 1-Wire Temperature Sensor [part_number=DS18B20]
  4k7_2 = 4k7 Ω Resistor [package=THT]
  4k7_3 = 4k7 Ω Resistor [package=THT]
  Part1 = Arduino Pro Mini v13
  S1 = Momentary Switch [package=ksa_sealed_tac_switch]
  S6 = Momentary Switch [package=ksa_sealed_tac_switch]
  S7 = Momentary Switch [package=ksa_sealed_tac_switch]
  S8 = Momentary Switch [package=ksa_sealed_tac_switch]
  S9 = Momentary Switch [package=ksa_sealed_tac_switch]
  U1 = TRANSISTOR_NPN_2 [package=to-92]
  R6 = Resistor [tolerance=±5% resistance=2.2k package=THT]
  R7 = Resistor [tolerance=±5% resistance=330 package=THT]
  R8 = Resistor [tolerance=±5% resistance=680 package=THT]
  R9 = Resistor [tolerance=±5% resistance=1k package=THT]
  R11 = 2k2 Ω Resistor [package=THT]
  R12 = Resistor [tolerance=±5% resistance=3.3k package=THT]
  J2 = Generic shrouded header - 10 pins [form="♂ (shrouded male)" package=THT]
  R13 = TRIMPOT [package=trimpot_pth_s3_lock]

nets:
  N1: LCD.VSS, LCD.R/W, LCD.LED-, S1.4, S9.2, U1.E, R13.CCW
  5V: LCD.VDD, DS2.VDD, DS1.VDD, 4k7.Pin_1, DS3.VDD, 4k7_2.Pin_1, 4k7_3.Pin_1, Part1.VCC, R6.Pin_1, R13.CW
  N2: LCD.V0, R13.WIPER
  N3: LCD.RS, Part1.A5
  N4: LCD.DB4, Part1.D4
  N5: LCD.DB7, Part1.D7
  N6: LCD.LED+, U1.C
  N7: DS2.DQ, 4k7.Pin_0, Part1.D2
  GND: DS2.GND, DS1.GND, DS3.GND, Part1.GND, J2.pin10
  N8: Rele.COIL2, Rele1.COIL2, Part1.A2, Part1.A1
  N9: DS1.DQ, 4k7_2.Pin_0, Part1.A3
  N10: DS3.DQ, 4k7_3.Pin_0, Part1.D9_PWM
  N11: Part1.A0, S1.1, R6.Pin_0, R7.Pin_1
  N12: Part1.D13/SCK, J2.pin6
  N13: Part1.D12/MISO, J2.pin4
  N14: Part1.D11_PWM/MOSI, J2.pin5
  N15: Part1.D10_PWM/SS, J2.pin3
  N16: Part1.D8, R11.Pin_0
  N17: Part1.RESET, J2.pin8
  N18: S6.1, R7.Pin_0, R8.Pin_1
  N19: S7.1, R8.Pin_0, R9.Pin_1
  N20: S8.1, R9.Pin_0, R12.Pin_1
  N21: S9.1, R12.Pin_0
  N22: U1.B, R11.Pin_1

notes:
  Saulės kolektoriaus valdiklis v1.2 controller v1.2
  Siurblio relė - pump relay
  solar collector controller with arduino pro mini processor, LCD screen and 2 temperature sensors DS18B20
  Termostatas -Thermostat
  Tinklo jungtis - network connector

custom parts:
  4k7 Ω Resistor: A generic resistor (0.25W)
  2k2 Ω Resistor: A generic resistor (0.25W)
  Generic shrouded header - 10 pins: Generic shrouded header
